# Fritzing sketch Driver-Display-v0.3 (saved by Fritzing 0.9.2b)
stripboards: 1

parts:
  J97 = female pin header, 6 pins [form="♀ (female)"]
  J98 = female pin header, 6 pins [form="♀ (female)"]
  J99 = female pin header, 6 pins [form="♀ (female)"]
  J100 = female pin header, 6 pins [form="♀ (female)"]
  J101 = female pin header, 6 pins [form="♀ (female)"]
  J102 = female pin header, 6 pins [form="♀ (female)"]
  J103 = female pin header, 6 pins [form="♀ (female)"]
  J104 = female pin header, 6 pins [form="♀ (female)"]
  J105 = female pin header, 6 pins [form="♀ (female)"]
  J106 = female pin header, 6 pins [form="♀ (female)"]
  J107 = female pin header, 6 pins [form="♀ (female)"]
  J108 = female pin header, 6 pins [form="♀ (female)"]
  J109 = male pin header, 7 pins [form="♂ (male)"]
  J110 = male pin header, 10 pins [form="♂ (male)"]
  NE-1 = Neon Bulb
  NE-2 = Neon Bulb
  NE-3 = Neon Bulb
  NE-4 = Neon Bulb
  NE-5 = Neon Bulb

nets:
  N1: J97.pin1, J109.pin6
  N2: J97.pin2, J99.pin2, J101.pin2, J103.pin2, J105.pin2, J107.pin2, J110.pin4, NE-2.B
  N3: J97.pin3, J99.pin3, J101.pin3, J103.pin3, J105.pin3, J107.pin3, J110.pin3, NE-3.B
  N4: J97.pin4, J99.pin4, J101.pin4, J103.pin4, J105.pin4, J107.pin4, J110.pin2, NE-4.B
  N5: J97.pin5, J99.pin5, J101.pin5, J103.pin5, J105.pin5, J107.pin5, J110.pin1, NE-5.B
  N6: J97.pin6, J99.pin6, J101.pin6, J103.pin6, J105.pin6, J107.pin6, J110.pin10
  N7: J98.pin2, J100.pin2, J102.pin2, J104.pin2, J106.pin2, J108.pin2, J110.pin6
  N8: J98.pin3, J100.pin3, J102.pin3, J104.pin3, J106.pin3, J108.pin3, J110.pin5, NE-1.B
  N9: J98.pin4, J100.pin4, J102.pin4, J104.pin4, J106.pin4, J108.pin4, J110.pin7
  N10: J98.pin5, J100.pin5, J102.pin5, J104.pin5, J106.pin5, J108.pin5, J110.pin8
  N11: J98.pin6, J100.pin6, J102.pin6, J104.pin6, J106.pin6, J108.pin6, J110.pin9
  N12: J99.pin1, J109.pin5
  N13: J101.pin1, J109.pin4
  N14: J103.pin1, J109.pin3
  N15: J105.pin1, J109.pin2
  N16: J107.pin1, J109.pin1
  N17: J109.pin7, NE-1.A, NE-2.A, NE-3.A, NE-4.A, NE-5.A

custom parts:
  Neon Bulb: Neon bulb
