# Fritzing sketch Driver-Logic-v0.3 (saved by Fritzing 0.9.2b)
stripboards: 1

parts:
  IC3 = IC, DIP package, 16 pins [chip_label=K155ID1]
  C3 = Ceramic Capacitor [capacitance=100nF package="100 mil [THT, multilayer]"]
  J11 = female pin header, 15 pins [form="♀ (female)"]
  J12 = female pin header, 5 pins [form="♀ (female)"]
  J13 = female pin header, 5 pins [form="♀ (female)"]

nets:
  N1: IC3.pin1, J12.pin4
  N2: IC3.pin2, J12.pin5
  N3: IC3.pin5, C3.1, J11.pin3
  N4: IC3.pin8, J13.pin3
  N5: IC3.pin9, J13.pin4
  N6: IC3.pin10, J12.pin3
  N7: IC3.pin11, J12.pin2
  N8: IC3.pin12, C3.0
  N9: IC3.pin13, J13.pin5
  N10: IC3.pin14, J12.pin1
  N11: IC3.pin15, J13.pin2
  N12: IC3.pin16, J13.pin1
