# Fritzing sketch Driver-Multiplexer-v0.3 (saved by Fritzing 0.9.2b)
stripboards: 1

parts:
  Q86 = PNP-Transistor [part_number=MPSA92 package="TO92 [THT]"]
  J27 = female pin header, 8 pins [form="♀ (female)" part_number="170v & anode header"]
  J28 = female pin header, 5 pins [form="♀ (female)" part_number="cathodes 0...4 [stacking header]"]  # not connected
  J29 = female pin header, 5 pins [form="♀ (female)" part_number="cathodes 5...9 [stacking header]"]  # not connected
  R174 = Resistor [tolerance=±5% resistance=390k package=THT]
  R175 = Resistor [tolerance=±5% resistance=5.6k package=THT]
  R176 = Resistor [tolerance=±5% resistance=390k package=THT]
  Q87 = NPN-Transistor [part_number=MPSA42 package="TO92 [THT]"]
  Q88 = NPN-Transistor [part_number=MPSA42 package="TO92 [THT]"]
  Q89 = PNP-Transistor [part_number=MPSA92 package="TO92 [THT]"]
  Q90 = PNP-Transistor [part_number=MPSA92 package="TO92 [THT]"]
  R177 = Resistor [tolerance=±5% resistance=5.6k package=THT]
  R178 = Resistor [tolerance=±5% resistance=5.6k package=THT]
  R179 = Resistor [tolerance=±5% resistance=15k package=THT]
  R180 = Resistor [tolerance=±5% resistance=5.6k package=THT]
  R181 = Resistor [tolerance=±5% resistance=10k power=0.25 package=THT]
  R182 = Resistor [tolerance=±5% resistance=390k package=THT]
  R183 = Resistor [tolerance=±5% resistance=390k package=THT]
  R184 = Resistor [tolerance=±5% resistance=390k package=THT]
  R185 = Resistor [tolerance=±5% resistance=15k package=THT]
  R186 = Resistor [tolerance=±5% resistance=5.6k package=THT]
  R187 = Resistor [tolerance=±5% resistance=5.6k package=THT]
  R188 = Resistor [tolerance=±5% resistance=10k power=0.25 package=THT]
  R189 = Resistor [tolerance=±5% resistance=15k package=THT]
  R190 = Resistor [tolerance=±5% resistance=390k package=THT]
  R191 = Resistor [tolerance=±5% resistance=10k power=0.25 package=THT]
  R192 = Resistor [tolerance=±5% resistance=15k package=THT]
  R193 = Resistor [tolerance=±5% resistance=390k package=THT]
  Q91 = NPN-Transistor [part_number=MPSA42 package="TO92 [THT]"]
  Q92 = PNP-Transistor [part_number=MPSA92 package="TO92 [THT]"]
  Q93 = NPN-Transistor [part_number=MPSA42 package="TO92 [THT]"]
  Q94 = NPN-Transistor [part_number=MPSA42 package="TO92 [THT]"]
  Q95 = PNP-Transistor [part_number=MPSA92 package="TO92 [THT]"]
  R194 = Resistor [tolerance=±5% resistance=10k power=0.25 package=THT]
  R195 = Resistor [tolerance=±5% resistance=15k package=THT]
  R196 = Resistor [tolerance=±5% resistance=5.6k package=THT]
  R197 = Resistor [tolerance=±5% resistance=15k package=THT]
  R198 = Resistor [tolerance=±5% resistance=10k power=0.25 package=THT]
  R199 = Resistor [tolerance=±5% resistance=390k package=THT]
  Q96 = PNP-Transistor [part_number=MPSA92 package="TO92 [THT]"]
  Q97 = PNP-Transistor [part_number=MPSA92 package="TO92 [THT]"]
  J30 = female pin header, 15 pins [form="♀ (female)" part_number="GPIO signalling [stacking header]"]
  R200 = Resistor [tolerance=±5% resistance=10k power=0.25 package=THT]
  Q98 = NPN-Transistor [part_number=MPSA42 package="TO92 [THT]"]
  Q99 = NPN-Transistor [part_number=MPSA42 package="TO92 [THT]"]
  R201 = Resistor [tolerance=±5% resistance=10k package=THT]

nets:
  N1: Q86.E, J27.pin1, R175.Pin_1, Q89.E, Q90.E, R177.Pin_1, R178.Pin_1, R180.Pin_1, R186.Pin_1, R187.Pin_1, Q92.E, Q95.E, R196.Pin_1, Q96.E, Q97.E
  N2: Q86.B, R177.Pin_0, R182.Pin_1
  N3: Q86.C, R179.Pin_0
  N4: J27.pin2, R195.Pin_1
  N5: J27.pin3, R189.Pin_1
  N6: J27.pin4, R197.Pin_1
  N7: J27.pin5, R192.Pin_1
  N8: J27.pin6, R179.Pin_1
  N9: J27.pin7, R185.Pin_1
  N10: J27.pin8, R174.Pin_1
  N11: R174.Pin_0, Q95.C
  N12: R175.Pin_0, R176.Pin_1, Q95.B
  N13: R176.Pin_0, Q99.C
  N14: Q87.E, Q88.E, Q91.E, Q93.E, Q94.E, J30.pin2, Q98.E, Q99.E
  N15: Q87.B, R194.Pin_0
  N16: Q87.C, R184.Pin_0
  N17: Q88.B, R181.Pin_0
  N18: Q88.C, R183.Pin_0
  N19: Q89.B, R178.Pin_0, R183.Pin_1
  N20: Q89.C, R197.Pin_0
  N21: Q90.B, R180.Pin_0, R184.Pin_1
  N22: Q90.C, R195.Pin_0
  N23: R181.Pin_1, J30.pin6
  N24: R182.Pin_0, Q98.C
  N25: R185.Pin_0, Q96.C
  N26: R186.Pin_0, R193.Pin_1, Q92.B
  N27: R187.Pin_0, R199.Pin_1, Q97.B
  N28: R188.Pin_0, J30.pin14
  N29: R188.Pin_1, Q93.B
  N30: R189.Pin_0, Q92.C
  N31: R190.Pin_0, Q93.C
  N32: R190.Pin_1, R196.Pin_0, Q96.B
  N33: R191.Pin_0, J30.pin5
  N34: R191.Pin_1, Q91.B
  N35: R192.Pin_0, Q97.C
  N36: R193.Pin_0, Q91.C
  N37: Q94.B, R198.Pin_1
  N38: Q94.C, R199.Pin_0
  N39: R194.Pin_1, J30.pin4
  N40: R198.Pin_0, J30.pin7
  N41: J30.pin13, R200.Pin_1
  N42: J30.pin15, R201.Pin_0
  N43: R200.Pin_0, Q98.B
  N44: Q99.B, R201.Pin_1
