# Fritzing sketch Driver-Power-v0.3 (saved by Fritzing 0.9.2b)
stripboards: 1

parts:
  R179 = Resistor [tolerance=±5% resistance=6.8k package=THT]
  R180 = Resistor [tolerance=±5% resistance=1M package=THT]
  R181 = Resistor [tolerance=±5% resistance=100k package=THT]
  J93 = female pin header, 6 pins [form="♀ (female)" part_number="HV module header"]
  U2 = mystery part, 3 pins [chip_label="1k multi turn pot" part_number="1k multi turn pot"]
  J94 = female pin header, 5 pins [form="♀ (female)" part_number="cathodes 0...4 [stacking header]"]  # not connected
  J95 = female pin header, 5 pins [form="♀ (female)" part_number="cathodes 5...9 [stacking header]"]  # not connected
  J96 = male pin header, 3 pins [form="♂ (male)" part_number="12v, GND, 5v power"]
  J97 = female pin header, 15 pins [form="♀ (female)" part_number="GPIO signalling [stacking header]"]
  J98 = female pin header, 8 pins [form="♀ (female)"]

nets:
  N1: R179.Pin_0, J93.pin3
  N2: R179.Pin_1, U2.pin1
  N3: R180.Pin_0, J93.pin5, U2.pin2, J96.pin2, J97.pin2
  N4: R180.Pin_1, R181.Pin_0, J93.pin4, J97.pin8
  N5: R181.Pin_1, J97.pin3
  N6: J93.pin1, J98.pin1
  N7: J93.pin6, J96.pin1
  N8: J96.pin3, J97.pin1
