# Fritzing sketch Nixie Circuit Design v0.2 (saved by Fritzing 0.9.2b)
circuit board: 8.46667cm x 5.64444cm
breadboards: 1
stripboards: 1

parts:
  Raspberry_Pi1 = Raspberry Pi 2
  Q1 = NPN-Transistor [part_number=MPSA42 package="TO92 [THT]"]
  Q2 = PNP-Transistor [part_number=MPSA92 package="TO92 [THT]"]
  R1 = Resistor [tolerance=±5% resistance=10k package=THT]
  R2 = Resistor [tolerance=±5% resistance=5.6k package=THT]
  R3 = Resistor [tolerance=±5% resistance=15k package=THT]
  R4 = Resistor [tolerance=±5% resistance=390k package=THT]
  IC1 = IC, DIP package, 16 pins [chip_label=K155ID1]
  Q3 = NPN-Transistor [part_number=MPSA42 package="TO92 [THT]"]
  Q4 = PNP-Transistor [part_number=MPSA92 package="TO92 [THT]"]
  R5 = Resistor [tolerance=±5% resistance=10k package=THT]
  R6 = Resistor [tolerance=±5% resistance=5.6k package=THT]
  R7 = Resistor [tolerance=±5% resistance=15k package=THT]
  R8 = Resistor [tolerance=±5% resistance=390k package=THT]
  Q5 = NPN-Transistor [part_number=MPSA42 package="TO92 [THT]"]
  Q6 = PNP-Transistor [part_number=MPSA92 package="TO92 [THT]"]
  R9 = Resistor [tolerance=±5% resistance=10k package=THT]
  R10 = Resistor [tolerance=±5% resistance=5.6k package=THT]
  R11 = Resistor [tolerance=±5% resistance=15k package=THT]
  R12 = Resistor [tolerance=±5% resistance=390k package=THT]
  Q7 = NPN-Transistor [part_number=MPSA42 package="TO92 [THT]"]
  Q8 = PNP-Transistor [part_number=MPSA92 package="TO92 [THT]"]
  R13 = Resistor [tolerance=±5% resistance=10k package=THT]
  R14 = Resistor [tolerance=±5% resistance=5.6k package=THT]
  R15 = Resistor [tolerance=±5% resistance=15k package=THT]
  R16 = Resistor [tolerance=±5% resistance=390k package=THT]
  Q9 = NPN-Transistor [part_number=MPSA42 package="TO92 [THT]"]
  Q10 = PNP-Transistor [part_number=MPSA92 package="TO92 [THT]"]
  R17 = Resistor [tolerance=±5% resistance=10k package=THT]
  R18 = Resistor [tolerance=±5% resistance=5.6k package=THT]
  R19 = Resistor [tolerance=±5% resistance=15k package=THT]
  R20 = Resistor [tolerance=±5% resistance=390k package=THT]
  Q11 = NPN-Transistor [part_number=MPSA42 package="TO92 [THT]"]
  Q12 = PNP-Transistor [part_number=MPSA92 package="TO92 [THT]"]
  R21 = Resistor [tolerance=±5% resistance=10k package=THT]
  R22 = Resistor [tolerance=±5% resistance=5.6k package=THT]
  R23 = Resistor [tolerance=±5% resistance=15k package=THT]
  R24 = Resistor [tolerance=±5% resistance=390k package=THT]
  LED1 = LED - 5mm [color="Red (633nm)" part_number=NEON package="5 mm [THT]"]
  LED2 = LED - 5mm [color="Red (633nm)" part_number=NEON package="5 mm [THT]"]
  LED3 = LED - 5mm [color="Red (633nm)" part_number=NEON package="5 mm [THT]"]
  LED4 = LED - 5mm [color="Red (633nm)" part_number=NEON package="5 mm [THT]"]
  LED5 = LED - 5mm [color="Red (633nm)" part_number=NEON package="5 mm [THT]"]
  Q13 = NPN-Transistor [part_number=MPSA42 package="TO92 [THT]"]
  Q14 = NPN-Transistor [part_number=MPSA42 package="TO92 [THT]"]
  Q15 = NPN-Transistor [part_number=MPSA42 package="TO92 [THT]"]
  Q16 = NPN-Transistor [part_number=MPSA42 package="TO92 [THT]"]
  Q17 = NPN-Transistor [part_number=MPSA42 package="TO92 [THT]"]
  R25 = Resistor [tolerance=±5% resistance=390k package=THT]
  R26 = Resistor [tolerance=±5% resistance=390k package=THT]
  R27 = Resistor [tolerance=±5% resistance=390k package=THT]
  R28 = Resistor [tolerance=±5% resistance=390k package=THT]
  R29 = Resistor [tolerance=±5% resistance=390k package=THT]
  J3 = double row female pin header, 12 pins [form="♀ (female)" part_number=nixie2]
  J4 = double row female pin header, 12 pins [form="♀ (female)" part_number=nixie3]
  J5 = double row female pin header, 12 pins [form="♀ (female)" part_number=nixie4]
  J6 = double row female pin header, 12 pins [form="♀ (female)" part_number=nixie5]
  J2 = female pin header, 12 pins [form="♀ (female)" part_number=nixie1]
  J7 = double row smd female pin header, 12 pins [form="♀ (female)" part_number=nixie6]
  R30 = Resistor [tolerance=±5% resistance=33k package=THT]
  R31 = Resistor [tolerance=±5% resistance=33k package=THT]
  R32 = Resistor [tolerance=±5% resistance=33k package=THT]
  R33 = Resistor [tolerance=±5% resistance=33k package=THT]
  R34 = Resistor [tolerance=±5% resistance=33k package=THT]
  C1 = Ceramic Capacitor [capacitance=100nF package="100 mil [THT, multilayer]"]
  R35 = Trimmer Potentiometer [maximum_resistance=1kΩ package=THT]
  R36 = Resistor [tolerance=±5% resistance=6.8k package=THT]
  JP1 = Header 4 [part_number=PSU package=molex-1x4_lock]
  J1 = female pin header, 6 pins [form="♀ (female)" part_number="HV Module"]

nets:
  3V3: Raspberry_Pi1.3v3, Raspberry_Pi1.3V3, IC1.pin5, C1.0
  N1: Raspberry_Pi1.GPIO2, R1.Pin_0
  N2: Raspberry_Pi1.GPIO3, R5.Pin_0
  N3: Raspberry_Pi1.GPIO4, R9.Pin_0
  N4: Raspberry_Pi1.GPIO17, R13.Pin_0
  N5: Raspberry_Pi1.GPIO27, R17.Pin_0
  N6: Raspberry_Pi1.GPIO22, R21.Pin_0
  N7: Raspberry_Pi1.GPIO20, IC1.pin3
  N8: Raspberry_Pi1.GPIO16, IC1.pin4
  N9: Raspberry_Pi1.GPIO12, IC1.pin6
  N10: Raspberry_Pi1.GND, Q1.E, IC1.pin12, Q3.E, Q5.E, Q7.E, Q9.E, Q11.E, Q13.E, Q14.E, Q15.E, Q16.E, Q17.E, C1.1
  N11: Raspberry_Pi1.GPIO7, IC1.pin7
  N12: Raspberry_Pi1.GPIO8, R30.Pin_0
  N13: Raspberry_Pi1.GPIO25, R31.Pin_0
  N14: Raspberry_Pi1.GPIO24, R32.Pin_0
  N15: Raspberry_Pi1.GPIO23, R33.Pin_0
  N16: Raspberry_Pi1.GPIO18, R34.Pin_0
  N17: Raspberry_Pi1.5V, JP1.4
  N18: Q1.B, R1.Pin_1
  N19: Q1.C, R4.Pin_0
  N20: Q2.E, R2.Pin_0, Q4.E, R6.Pin_0, Q6.E, R10.Pin_0, Q8.E, R14.Pin_0, Q10.E, R18.Pin_0, Q12.E, R22.Pin_0, R25.Pin_0, R26.Pin_0, R27.Pin_0, R28.Pin_0, R29.Pin_0, J1.pin6
  N21: Q2.B, R2.Pin_1, R4.Pin_1
  N22: Q2.C, R3.Pin_0
  N23: R3.Pin_1, J2.pin1
  N24: IC1.pin1, J3.pin7, J4.pin7, J5.pin7, J6.pin7, J2.pin7, J7.pin7
  N25: IC1.pin2, J3.pin6, J4.pin6, J5.pin6, J6.pin6, J2.pin6, J7.pin6
  N26: IC1.pin8, J3.pin3, J4.pin3, J5.pin3, J6.pin3, J2.pin3, J7.pin3
  N27: IC1.pin9, J3.pin2, J4.pin2, J5.pin2, J6.pin2, J2.pin2, J7.pin2
  N28: IC1.pin10, J3.pin8, J4.pin8, J5.pin8, J6.pin8, J2.pin8, J7.pin8
  N29: IC1.pin11, J3.pin9, J4.pin9, J5.pin9, J6.pin9, J2.pin9, J7.pin9
  N30: IC1.pin13, J3.pin10, J4.pin10, J5.pin10, J6.pin10, J2.pin10, J7.pin10
  N31: IC1.pin14, J3.pin11, J4.pin11, J5.pin11, J6.pin11, J2.pin11, J7.pin11
  N32: IC1.pin15, J3.pin4, J4.pin4, J5.pin4, J6.pin4, J2.pin4, J7.pin4
  N33: IC1.pin16, J3.pin5, J4.pin5, J5.pin5, J6.pin5, J2.pin5, J7.pin5
  N34: Q3.B, R5.Pin_1
  N35: Q3.C, R8.Pin_0
  N36: Q4.B, R6.Pin_1, R8.Pin_1
  N37: Q4.C, R7.Pin_0
  N38: R7.Pin_1, J3.pin1
  N39: Q5.B, R9.Pin_1
  N40: Q5.C, R12.Pin_0
  N41: Q6.B, R10.Pin_1, R12.Pin_1
  N42: Q6.C, R11.Pin_0
  N43: R11.Pin_1, J4.pin1
  N44: Q7.B, R13.Pin_1
  N45: Q7.C, R16.Pin_0
  N46: Q8.B, R14.Pin_1, R16.Pin_1
  N47: Q8.C, R15.Pin_0
  N48: R15.Pin_1, J5.pin1
  N49: Q9.B, R17.Pin_1
  N50: Q9.C, R20.Pin_0
  N51: Q10.B, R18.Pin_1, R20.Pin_1
  N52: Q10.C, R19.Pin_0
  N53: R19.Pin_1, J6.pin1
  N54: Q11.B, R21.Pin_1
  N55: Q11.C, R24.Pin_0
  N56: Q12.B, R22.Pin_1, R24.Pin_1
  N57: Q12.C, R23.Pin_0
  N58: R23.Pin_1, J7.pin1
  N59: LED1.cathode, Q14.C
  N60: LED1.anode, R29.Pin_1
  N61: LED2.cathode, Q15.C
  N62: LED2.anode, R28.Pin_1
  N63: LED3.cathode, Q17.C
  N64: LED3.anode, R26.Pin_1
  N65: LED4.cathode, Q16.C
  N66: LED4.anode, R27.Pin_1
  N67: LED5.cathode, Q13.C
  N68: LED5.anode, R25.Pin_1
  N69: Q13.B, R30.Pin_1
  N70: Q14.B, R34.Pin_1
  N71: Q15.B, R33.Pin_1
  N72: Q16.B, R32.Pin_1
  N73: Q17.B, R31.Pin_1
  N74: R35.wiper, R36.Pin_1
  N75: R35.leg2, JP1.2, JP1.3, J1.pin2, J1.pin3, J1.pin5
  N76: R36.Pin_0, J1.pin4
  N77: JP1.1, J1.pin1
