# Fritzing sketch Nixie Circuit Design v0.3 (saved by Fritzing 0.9.2b)
stripboards: 9

parts:
  IC2 = IC, DIP package, 16 pins [chip_label=K155ID1]
  C2 = Ceramic Capacitor [capacitance=100nF package="100 mil [THT, multilayer]"]
  J9 = female pin header, 5 pins [form="♀ (female)"]
  J10 = female pin header, 5 pins [form="♀ (female)"]
  J8 = female pin header, 15 pins [form="♀ (female)"]
  J19 = female pin header, 15 pins [form="♀ (female)" part_number="GPIO signalling [stacking header]"]
  Q58 = PNP-Transistor [part_number=MPSA92 package="TO92 [THT]"]
  Q59 = NPN-Transistor [part_number=MPSA42 package="TO92 [THT]"]
  Q60 = NPN-Transistor [part_number=MPSA42 package="TO92 [THT]"]
  Q61 = PNP-Transistor [part_number=MPSA92 package="TO92 [THT]"]
  Q62 = PNP-Transistor [part_number=MPSA92 package="TO92 [THT]"]
  Q63 = NPN-Transistor [part_number=MPSA42 package="TO92 [THT]"]
  R118 = Resistor [tolerance=±5% resistance=390k package=THT]
  R119 = Resistor [tolerance=±5% resistance=15k package=THT]
  R120 = Resistor [tolerance=±5% resistance=10k power=0.25 package=THT]
  R121 = Resistor [tolerance=±5% resistance=390k package=THT]
  R122 = Resistor [tolerance=±5% resistance=390k package=THT]
  R123 = Resistor [tolerance=±5% resistance=15k package=THT]
  R124 = Resistor [tolerance=±5% resistance=10k power=0.25 package=THT]
  R125 = Resistor [tolerance=±5% resistance=10k power=0.25 package=THT]
  R126 = Resistor [tolerance=±5% resistance=15k package=THT]
  R127 = Resistor [tolerance=±5% resistance=5.6k package=THT]
  R128 = Resistor [tolerance=±5% resistance=5.6k package=THT]
  R129 = Resistor [tolerance=±5% resistance=15k package=THT]
  R130 = Resistor [tolerance=±5% resistance=5.6k package=THT]
  R131 = Resistor [tolerance=±5% resistance=390k package=THT]
  R132 = Resistor [tolerance=±5% resistance=390k package=THT]
  R133 = Resistor [tolerance=±5% resistance=390k package=THT]
  R134 = Resistor [tolerance=±5% resistance=10k power=0.25 package=THT]
  R135 = Resistor [tolerance=±5% resistance=5.6k package=THT]
  R136 = Resistor [tolerance=±5% resistance=15k package=THT]
  R137 = Resistor [tolerance=±5% resistance=15k package=THT]
  R138 = Resistor [tolerance=±5% resistance=5.6k package=THT]
  R139 = Resistor [tolerance=±5% resistance=10k power=0.25 package=THT]
  R140 = Resistor [tolerance=±5% resistance=10k power=0.25 package=THT]
  R141 = Resistor [tolerance=±5% resistance=5.6k package=THT]
  Q64 = PNP-Transistor [part_number=MPSA92 package="TO92 [THT]"]
  Q65 = PNP-Transistor [part_number=MPSA92 package="TO92 [THT]"]
  Q66 = NPN-Transistor [part_number=MPSA42 package="TO92 [THT]"]
  Q67 = PNP-Transistor [part_number=MPSA92 package="TO92 [THT]"]
  Q68 = NPN-Transistor [part_number=MPSA42 package="TO92 [THT]"]
  Q69 = NPN-Transistor [part_number=MPSA42 package="TO92 [THT]"]
  Q70 = NPN-Transistor [part_number=MPSA42 package="TO92 [THT]"]
  Q71 = PNP-Transistor [part_number=MPSA92 package="TO92 [THT]"]
  R142 = Resistor [tolerance=±5% resistance=390k package=THT]
  R143 = Resistor [tolerance=±5% resistance=10k package=THT]
  R144 = Resistor [tolerance=±5% resistance=5.6k package=THT]
  R145 = Resistor [tolerance=±5% resistance=390k package=THT]
  J20 = female pin header, 5 pins [form="♀ (female)" part_number="cathodes 5...9 [stacking header]"]  # not connected
  J21 = female pin header, 5 pins [form="♀ (female)" part_number="cathodes 0...4 [stacking header]"]  # not connected
  J22 = female pin header, 8 pins [form="♀ (female)" part_number="170v & anode header"]  # not connected
  Q72 = PNP-Transistor [part_number=MPSA92 package="TO92 [THT]"]
  Q73 = NPN-Transistor [part_number=MPSA42 package="TO92 [THT]"]
  Q74 = NPN-Transistor [part_number=MPSA42 package="TO92 [THT]"]
  Q75 = PNP-Transistor [part_number=MPSA92 package="TO92 [THT]"]
  Q76 = PNP-Transistor [part_number=MPSA92 package="TO92 [THT]"]
  Q77 = NPN-Transistor [part_number=MPSA42 package="TO92 [THT]"]
  R146 = Resistor [tolerance=±5% resistance=390k package=THT]
  R147 = Resistor [tolerance=±5% resistance=15k package=THT]
  R148 = Resistor [tolerance=±5% resistance=10k power=0.25 package=THT]
  R149 = Resistor [tolerance=±5% resistance=390k package=THT]
  R150 = Resistor [tolerance=±5% resistance=390k package=THT]
  R151 = Resistor [tolerance=±5% resistance=15k package=THT]
  R152 = Resistor [tolerance=±5% resistance=10k power=0.25 package=THT]
  R153 = Resistor [tolerance=±5% resistance=10k power=0.25 package=THT]
  R154 = Resistor [tolerance=±5% resistance=15k package=THT]
  R155 = Resistor [tolerance=±5% resistance=5.6k package=THT]
  R156 = Resistor [tolerance=±5% resistance=5.6k package=THT]
  R157 = Resistor [tolerance=±5% resistance=15k package=THT]
  R158 = Resistor [tolerance=±5% resistance=5.6k package=THT]
  R159 = Resistor [tolerance=±5% resistance=390k package=THT]
  R160 = Resistor [tolerance=±5% resistance=390k package=THT]
  R161 = Resistor [tolerance=±5% resistance=390k package=THT]
  R162 = Resistor [tolerance=±5% resistance=10k power=0.25 package=THT]
  R163 = Resistor [tolerance=±5% resistance=5.6k package=THT]
  R164 = Resistor [tolerance=±5% resistance=15k package=THT]
  R165 = Resistor [tolerance=±5% resistance=15k package=THT]
  R166 = Resistor [tolerance=±5% resistance=5.6k package=THT]
  R167 = Resistor [tolerance=±5% resistance=10k power=0.25 package=THT]
  R168 = Resistor [tolerance=±5% resistance=10k power=0.25 package=THT]
  R169 = Resistor [tolerance=±5% resistance=5.6k package=THT]
  Q78 = PNP-Transistor [part_number=MPSA92 package="TO92 [THT]"]
  Q79 = PNP-Transistor [part_number=MPSA92 package="TO92 [THT]"]
  Q80 = NPN-Transistor [part_number=MPSA42 package="TO92 [THT]"]
  Q81 = PNP-Transistor [part_number=MPSA92 package="TO92 [THT]"]
  Q82 = NPN-Transistor [part_number=MPSA42 package="TO92 [THT]"]
  Q83 = NPN-Transistor [part_number=MPSA42 package="TO92 [THT]"]
  Q84 = NPN-Transistor [part_number=MPSA42 package="TO92 [THT]"]
  Q85 = PNP-Transistor [part_number=MPSA92 package="TO92 [THT]"]
  R170 = Resistor [tolerance=±5% resistance=390k package=THT]
  R171 = Resistor [tolerance=±5% resistance=10k package=THT]
  R172 = Resistor [tolerance=±5% resistance=5.6k package=THT]
  R173 = Resistor [tolerance=±5% resistance=390k package=THT]
  J24 = female pin header, 5 pins [form="♀ (female)" part_number="cathodes 5...9 [stacking header]"]  # not connected
  J25 = female pin header, 5 pins [form="♀ (female)" part_number="cathodes 0...4 [stacking header]"]  # not connected
  J26 = female pin header, 8 pins [form="♀ (female)" part_number="170v & anode header"]
  J23 = female pin header, 15 pins [form="♀ (female)" part_number="GPIO signalling [stacking header]"]
  J31 = female pin header, 6 pins [form="♀ (female)" part_number="HV module header"]
  U1 = mystery part, 3 pins [chip_label=? part_number="1k multi turn pot"]
  J33 = female pin header, 5 pins [form="♀ (female)" part_number="cathodes 5...9 [stacking header]"]  # not connected
  J34 = female pin header, 5 pins [form="♀ (female)" part_number="cathodes 0...4 [stacking header]"]  # not connected
  J36 = male pin header, 3 pins [form="♂ (male)" part_number="12v, GND, 5v power"]
  J37 = female pin header, 6 pins [form="♀ (female)"]  # not connected
  J38 = female pin header, 6 pins [form="♀ (female)"]  # not connected
  J39 = female pin header, 6 pins [form="♀ (female)"]  # not connected
  J40 = female pin header, 6 pins [form="♀ (female)"]  # not connected
  J41 = female pin header, 6 pins [form="♀ (female)"]  # not connected
  J42 = female pin header, 6 pins [form="♀ (female)"]  # not connected
  J43 = female pin header, 6 pins [form="♀ (female)"]  # not connected
  J44 = female pin header, 6 pins [form="♀ (female)"]  # not connected
  J45 = female pin header, 6 pins [form="♀ (female)"]  # not connected
  J46 = female pin header, 6 pins [form="♀ (female)"]  # not connected
  J47 = female pin header, 6 pins [form="♀ (female)"]  # not connected
  J48 = female pin header, 6 pins [form="♀ (female)"]  # not connected
  NE-1 = Neon Bulb
  NE-2 = Neon Bulb  # not connected
  NE-3 = Neon Bulb  # not connected
  NE-4 = Neon Bulb  # not connected
  NE-5 = Neon Bulb  # not connected
  J51 = female pin header, 6 pins [form="♀ (female)"]
  J52 = female pin header, 6 pins [form="♀ (female)"]
  J53 = female pin header, 6 pins [form="♀ (female)"]
  J54 = female pin header, 6 pins [form="♀ (female)"]
  J55 = female pin header, 6 pins [form="♀ (female)"]
  J56 = female pin header, 6 pins [form="♀ (female)"]
  J57 = female pin header, 6 pins [form="♀ (female)"]
  J58 = female pin header, 6 pins [form="♀ (female)"]
  J59 = female pin header, 6 pins [form="♀ (female)"]
  J60 = female pin header, 6 pins [form="♀ (female)"]
  J61 = female pin header, 6 pins [form="♀ (female)"]
  J62 = female pin header, 6 pins [form="♀ (female)"]
  NE-6 = Neon Bulb
  NE-7 = Neon Bulb
  NE-8 = Neon Bulb
  NE-9 = Neon Bulb
  NE-10 = Neon Bulb
  R176 = Resistor [tolerance=±5% resistance=6.8k package=THT]
  R177 = Resistor [tolerance=±5% resistance=1M package=THT]
  R178 = Resistor [tolerance=±5% resistance=100k package=THT]
  J65 = female pin header, 10 pins [form="♀ (female)"]  # not connected
  J66 = female pin header, 5 pins [form="♀ (female)"]  # not connected
  J67 = female pin header, 8 pins [form="♀ (female)"]  # not connected
  J68 = female pin header, 1 pin [form="♀ (female)"]  # not connected
  J69 = female pin header, 5 pins [form="♀ (female)"]  # not connected
  J70 = female pin header, 4 pins [form="♀ (female)"]  # not connected
  J71 = female pin header, 5 pins [form="♀ (female)"]  # not connected
  J72 = female pin header, 4 pins [form="♀ (female)"]  # not connected
  J73 = female pin header, 10 pins [form="♀ (female)"]  # not connected
  J74 = female pin header, 8 pins [form="♀ (female)"]  # not connected
  J75 = female pin header, 5 pins [form="♀ (female)"]  # not connected
  J76 = female pin header, 5 pins [form="♀ (female)"]  # not connected
  J77 = female pin header, 1 pin [form="♀ (female)"]  # not connected
  J78 = female pin header, 4 pins [form="♀ (female)"]  # not connected
  J79 = female pin header, 4 pins [form="♀ (female)"]  # not connected
  J80 = female pin header, 4 pins [form="♀ (female)"]  # not connected
  J81 = female pin header, 4 pins [form="♀ (female)"]  # not connected
  J82 = female pin header, 5 pins [form="♀ (female)"]  # not connected
  R179 = Resistor [tolerance=±5% resistance=6.8k package=THT]
  R180 = Resistor [tolerance=±5% resistance=1M package=THT]
  R181 = Resistor [tolerance=±5% resistance=100k package=THT]
  J83 = male pin header, 15 pins [form="♂ (male)" part_number="GPIO signalling header"]
  J84 = male pin header, 5 pins [form="♂ (male)" part_number="cathodes 5...9 header"]
  J85 = male pin header, 5 pins [form="♂ (male)" part_number="cathodes 0...4 header"]
  J86 = male pin header, 8 pins [form="♂ (male)" part_number="170v & anode header"]
  J87 = female pin header, 6 pins [form="♀ (female)" part_number="HV module header"]
  U2 = mystery part, 3 pins [chip_label=? part_number="1k multi turn pot"]
  J88 = female pin header, 5 pins [form="♀ (female)" part_number="cathode header"]
  J89 = female pin header, 5 pins [form="♀ (female)" part_number="cathode header"]
  J90 = female pin header, 7 pins [form="♀ (female)" part_number="anode header"]
  J91 = male pin header, 3 pins [form="♂ (male)" part_number="12v, GND, 5v power"]
  J92 = female pin header, 15 pins [form="♀ (female)" part_number="GPIO signalling [stacking header]"]
  J35 = female pin header, 8 pins [form="♀ (female)"]
  J93 = male pin header, 7 pins [form="♂ (male)"]
  J94 = male pin header, 10 pins [form="♂ (male)"]  # not connected
  J95 = male pin header, 7 pins [form="♂ (male)"]
  J96 = male pin header, 10 pins [form="♂ (male)"]
  J109 = male pin header, 7 pins [form="♂ (male)"]  # not connected
  J110 = male pin header, 10 pins [form="♂ (male)"]  # not connected

nets:
  N1: IC2.pin1, J9.pin4
  N2: IC2.pin2, J9.pin5
  N3: IC2.pin5, C2.1, J8.pin3
  N4: IC2.pin8, J10.pin3
  N5: IC2.pin9, J10.pin4
  N6: IC2.pin10, J9.pin3
  N7: IC2.pin11, J9.pin2
  N8: IC2.pin12, C2.0
  N9: IC2.pin13, J10.pin5
  N10: IC2.pin14, J9.pin1
  N11: IC2.pin15, J10.pin2
  N12: IC2.pin16, J10.pin1
  N13: J19.pin6, R134.Pin_1
  N14: J19.pin7, R124.Pin_0
  N15: J19.pin13, R140.Pin_1
  N16: J19.pin14, R125.Pin_0
  N17: J19.pin15, R143.Pin_0
  N18: Q58.E, R127.Pin_1
  N19: Q58.B, R121.Pin_1, R127.Pin_0
  N20: Q58.C, R119.Pin_0
  N21: Q59.B, R124.Pin_1
  N22: Q59.C, R121.Pin_0
  N23: Q60.B, R125.Pin_1
  N24: Q60.C, R122.Pin_0
  N25: Q61.E, R130.Pin_1
  N26: Q61.B, R122.Pin_1, R130.Pin_0
  N27: Q61.C, R129.Pin_0
  N28: Q62.E, R128.Pin_1
  N29: Q62.B, R118.Pin_1, R128.Pin_0
  N30: Q62.C, R123.Pin_0
  N31: Q63.B, R120.Pin_1
  N32: Q63.C, R118.Pin_0
  N33: R126.Pin_0, Q65.C
  N34: R131.Pin_0, Q69.C
  N35: R131.Pin_1, R135.Pin_0, Q64.B
  N36: R132.Pin_0, Q66.C
  N37: R132.Pin_1, R138.Pin_0, Q65.B
  N38: R133.Pin_0, Q68.C
  N39: R133.Pin_1, R141.Pin_0, Q67.B
  N40: R134.Pin_0, Q66.B
  N41: R135.Pin_1, Q64.E
  N42: R136.Pin_0, Q64.C
  N43: R137.Pin_0, Q67.C
  N44: R138.Pin_1, Q65.E
  N45: R139.Pin_0, Q69.B
  N46: R140.Pin_0, Q68.B
  N47: R141.Pin_1, Q67.E
  N48: Q70.B, R143.Pin_1
  N49: Q70.C, R142.Pin_0
  N50: Q71.E, R144.Pin_1
  N51: Q71.B, R142.Pin_1, R144.Pin_0
  N52: Q71.C, R145.Pin_0
  N53: Q72.E, Q75.E, Q76.E, R155.Pin_1, R156.Pin_1, R158.Pin_1, R163.Pin_1, R166.Pin_1, R169.Pin_1, Q78.E, Q79.E, Q81.E, Q85.E, R172.Pin_1, J26.pin1
  N54: Q72.B, R149.Pin_1, R155.Pin_0
  N55: Q72.C, R147.Pin_0
  N56: Q73.E, Q74.E, Q77.E, Q80.E, Q82.E, Q83.E, Q84.E, J23.pin2
  N57: Q73.B, R152.Pin_1
  N58: Q73.C, R149.Pin_0
  N59: Q74.B, R153.Pin_1
  N60: Q74.C, R150.Pin_0
  N61: Q75.B, R150.Pin_1, R158.Pin_0
  N62: Q75.C, R157.Pin_0
  N63: Q76.B, R146.Pin_1, R156.Pin_0
  N64: Q76.C, R151.Pin_0
  N65: Q77.B, R148.Pin_1
  N66: Q77.C, R146.Pin_0
  N67: R147.Pin_1, J26.pin5
  N68: R148.Pin_0, J23.pin5
  N69: R151.Pin_1, J26.pin3
  N70: R152.Pin_0, J23.pin7
  N71: R153.Pin_0, J23.pin14
  N72: R154.Pin_0, Q79.C
  N73: R154.Pin_1, J26.pin4
  N74: R157.Pin_1, J26.pin7
  N75: R159.Pin_0, Q83.C
  N76: R159.Pin_1, R163.Pin_0, Q78.B
  N77: R160.Pin_0, Q80.C
  N78: R160.Pin_1, R166.Pin_0, Q79.B
  N79: R161.Pin_0, Q82.C
  N80: R161.Pin_1, R169.Pin_0, Q81.B
  N81: R162.Pin_0, Q80.B
  N82: R162.Pin_1, J23.pin6
  N83: R164.Pin_0, Q78.C
  N84: R164.Pin_1, J26.pin2
  N85: R165.Pin_0, Q81.C
  N86: R165.Pin_1, J26.pin6
  N87: R167.Pin_0, Q83.B
  N88: R167.Pin_1, J23.pin4
  N89: R168.Pin_0, Q82.B
  N90: R168.Pin_1, J23.pin13
  N91: Q84.B, R171.Pin_1
  N92: Q84.C, R170.Pin_0
  N93: Q85.B, R170.Pin_1, R172.Pin_0
  N94: Q85.C, R173.Pin_0
  N95: R171.Pin_0, J23.pin15
  N96: R173.Pin_1, J26.pin8
  N97: J31.pin1, J35.pin1
  N98: J31.pin3, R176.Pin_0
  N99: J31.pin4, R177.Pin_1, R178.Pin_0, J92.pin8
  N100: J31.pin5, U1.pin2, J36.pin2, R177.Pin_0, J92.pin2
  N101: J31.pin6, J36.pin1
  N102: U1.pin1, R176.Pin_1
  N103: J36.pin3, J92.pin1
  N104: NE-1.A, J93.pin7
  N105: J51.pin1, J95.pin6
  N106: J51.pin2, J53.pin2, J55.pin2, J57.pin2, J59.pin2, J61.pin2, NE-8.B, J96.pin4
  N107: J51.pin3, J53.pin3, J55.pin3, J57.pin3, J59.pin3, J61.pin3, NE-9.B, J96.pin3
  N108: J51.pin4, J53.pin4, J55.pin4, J57.pin4, J59.pin4, J61.pin4, NE-7.B, J96.pin2
  N109: J51.pin5, J53.pin5, J55.pin5, J57.pin5, J59.pin5, J61.pin5, NE-6.B, J96.pin1
  N110: J51.pin6, J53.pin6, J55.pin6, J57.pin6, J59.pin6, J61.pin6, J96.pin10
  N111: J52.pin2, J54.pin2, J56.pin2, J58.pin2, J60.pin2, J62.pin2, J96.pin6
  N112: J52.pin3, J54.pin3, J56.pin3, J58.pin3, J60.pin3, J62.pin3, NE-10.B, J96.pin5
  N113: J52.pin4, J54.pin4, J56.pin4, J58.pin4, J60.pin4, J62.pin4, J96.pin7
  N114: J52.pin5, J54.pin5, J56.pin5, J58.pin5, J60.pin5, J62.pin5, J96.pin8
  N115: J52.pin6, J54.pin6, J56.pin6, J58.pin6, J60.pin6, J62.pin6, J96.pin9
  N116: J53.pin1, J95.pin5
  N117: J55.pin1, J95.pin4
  N118: J57.pin1, J95.pin3
  N119: J59.pin1, J95.pin2
  N120: J61.pin1, J95.pin1
  N121: NE-6.A, NE-7.A, NE-8.A, NE-9.A, NE-10.A, J95.pin7
  N122: R178.Pin_1, J92.pin3
  N123: R179.Pin_0, J87.pin3
  N124: R179.Pin_1, U2.pin1
  N125: R180.Pin_0, J83.pin2, J87.pin5, U2.pin2, J91.pin2
  N126: R180.Pin_1, R181.Pin_0, J83.pin8, J87.pin4
  N127: R181.Pin_1, J83.pin3
  N128: J83.pin1, J91.pin3
  N129: J84.pin1, J89.pin1
  N130: J84.pin2, J84.pin3, J89.pin2, J89.pin3
  N131: J84.pin4, J89.pin4
  N132: J84.pin5, J89.pin5
  N133: J85.pin1, J88.pin1
  N134: J85.pin2, J88.pin2
  N135: J85.pin3, J88.pin3
  N136: J85.pin4, J88.pin4
  N137: J85.pin5, J88.pin5
  N138: J86.pin1, J87.pin1
  N139: J86.pin2, J90.pin1
  N140: J86.pin3, J90.pin2
  N141: J86.pin4, J90.pin3
  N142: J86.pin5, J90.pin4
  N143: J86.pin6, J90.pin5
  N144: J86.pin7, J90.pin6
  N145: J86.pin8, J90.pin7
  N146: J87.pin6, J91.pin1

custom parts:
  Neon Bulb: Neon bulb
