# Fritzing sketch Nixie Circuit Design (saved by Fritzing 0.9.2b)
breadboards: 1

parts:
  Raspberry_Pi1 = Raspberry Pi 2
  Q1 = NPN-Transistor [part_number=MPSA42 package="TO92 [THT]"]
  Q2 = PNP-Transistor [part_number=MPSA92 package="TO92 [THT]"]
  R1 = Resistor [tolerance=±5% resistance=10k package=THT]
  R2 = Resistor [tolerance=±5% resistance=5.6k package=THT]
  R3 = Resistor [tolerance=±5% resistance=15k package=THT]
  R4 = Resistor [tolerance=±5% resistance=390k package=THT]
  IC1 = IC, DIP package, 16 pins [chip_label=K155ID1]
  Q3 = NPN-Transistor [part_number=MPSA42 package="TO92 [THT]"]
  Q4 = PNP-Transistor [part_number=MPSA92 package="TO92 [THT]"]
  R5 = Resistor [tolerance=±5% resistance=10k package=THT]  # not connected
  R6 = Resistor [tolerance=±5% resistance=5.6k package=THT]
  R7 = Resistor [tolerance=±5% resistance=15k package=THT]
  R8 = Resistor [tolerance=±5% resistance=390k package=THT]
  Q5 = NPN-Transistor [part_number=MPSA42 package="TO92 [THT]"]
  Q6 = PNP-Transistor [part_number=MPSA92 package="TO92 [THT]"]
  R9 = Resistor [tolerance=±5% resistance=10k package=THT]  # not connected
  R10 = Resistor [tolerance=±5% resistance=5.6k package=THT]
  R11 = Resistor [tolerance=±5% resistance=15k package=THT]
  R12 = Resistor [tolerance=±5% resistance=390k package=THT]
  Q7 = NPN-Transistor [part_number=MPSA42 package="TO92 [THT]"]
  Q8 = PNP-Transistor [part_number=MPSA92 package="TO92 [THT]"]
  R13 = Resistor [tolerance=±5% resistance=10k package=THT]  # not connected
  R14 = Resistor [tolerance=±5% resistance=5.6k package=THT]
  R15 = Resistor [tolerance=±5% resistance=15k package=THT]
  R16 = Resistor [tolerance=±5% resistance=390k package=THT]
  Q9 = NPN-Transistor [part_number=MPSA42 package="TO92 [THT]"]
  Q10 = PNP-Transistor [part_number=MPSA92 package="TO92 [THT]"]
  R17 = Resistor [tolerance=±5% resistance=10k package=THT]  # not connected
  R18 = Resistor [tolerance=±5% resistance=5.6k package=THT]
  R19 = Resistor [tolerance=±5% resistance=15k package=THT]
  R20 = Resistor [tolerance=±5% resistance=390k package=THT]
  Q11 = NPN-Transistor [part_number=MPSA42 package="TO92 [THT]"]
  Q12 = PNP-Transistor [part_number=MPSA92 package="TO92 [THT]"]
  R21 = Resistor [tolerance=±5% resistance=10k package=THT]  # not connected
  R22 = Resistor [tolerance=±5% resistance=5.6k package=THT]
  R23 = Resistor [tolerance=±5% resistance=15k package=THT]
  R24 = Resistor [tolerance=±5% resistance=390k package=THT]
  LED1 = LED - 5mm [color="Red (633nm)" part_number=NEON package="5 mm [THT]"]  # not connected
  LED2 = LED - 5mm [color="Red (633nm)" part_number=NEON package="5 mm [THT]"]  # not connected
  LED3 = LED - 5mm [color="Red (633nm)" part_number=NEON package="5 mm [THT]"]  # not connected
  LED4 = LED - 5mm [color="Red (633nm)" part_number=NEON package="5 mm [THT]"]  # not connected
  LED5 = LED - 5mm [color="Red (633nm)" part_number=NEON package="5 mm [THT]"]  # not connected
  Q13 = NPN-Transistor [part_number=MPSA42 package="TO92 [THT]"]  # not connected
  Q14 = NPN-Transistor [part_number=MPSA42 package="TO92 [THT]"]  # not connected
  Q15 = NPN-Transistor [part_number=MPSA42 package="TO92 [THT]"]  # not connected
  Q16 = NPN-Transistor [part_number=MPSA42 package="TO92 [THT]"]  # not connected
  Q17 = NPN-Transistor [part_number=MPSA42 package="TO92 [THT]"]  # not connected
  R25 = Resistor [tolerance=±5% resistance=390k package=THT]  # not connected
  R26 = Resistor [tolerance=±5% resistance=390k package=THT]  # not connected
  R27 = Resistor [tolerance=±5% resistance=390k package=THT]  # not connected
  R28 = Resistor [tolerance=±5% resistance=390k package=THT]  # not connected
  R29 = Resistor [tolerance=±5% resistance=390k package=THT]  # not connected
  J3 = double row female pin header, 12 pins [form="♀ (female)" part_number=nixie2]
  J4 = double row female pin header, 12 pins [form="♀ (female)" part_number=nixie3]
  J5 = double row female pin header, 12 pins [form="♀ (female)" part_number=nixie4]
  J6 = double row female pin header, 12 pins [form="♀ (female)" part_number=nixie5]
  J2 = female pin header, 12 pins [form="♀ (female)" part_number=nixie1]
  J7 = double row smd female pin header, 12 pins [form="♀ (female)" part_number=nixie6]
  J1 = single row smd female pin header, 6 pins [form="♀ (female)" part_number="HV module"]  # not connected

nets:
  3V3: Raspberry_Pi1.3v3, Raspberry_Pi1.3V3, IC1.pin5
  N1: Raspberry_Pi1.GPIO10, IC1.pin7
  N2: Raspberry_Pi1.GPIO9, IC1.pin4
  N3: Raspberry_Pi1.GND, Q1.E, IC1.pin12, Q3.E, Q5.E, Q7.E, Q9.E, Q11.E
  N4: Raspberry_Pi1.GPIO7, IC1.pin6
  N5: Raspberry_Pi1.GPIO8, IC1.pin3
  N6: Q1.B, R1.Pin_1
  N7: Q1.C, R4.Pin_0
  N8: Q2.E, R2.Pin_0, Q4.E, R6.Pin_0, Q6.E, R10.Pin_0, Q8.E, R14.Pin_0, Q10.E, R18.Pin_0, Q12.E, R22.Pin_0
  N9: Q2.B, R2.Pin_1, R4.Pin_1
  N10: Q2.C, R3.Pin_0
  N11: R3.Pin_1, J2.pin1
  N12: IC1.pin1, J3.pin7, J4.pin7, J5.pin7, J6.pin7, J2.pin7, J7.pin7
  N13: IC1.pin2, J3.pin6, J4.pin6, J5.pin6, J6.pin6, J2.pin6, J7.pin6
  N14: IC1.pin8, J3.pin3, J4.pin3, J5.pin3, J6.pin3, J2.pin3, J7.pin3
  N15: IC1.pin9, J3.pin2, J4.pin2, J5.pin2, J6.pin2, J2.pin2, J7.pin2
  N16: IC1.pin10, J3.pin8, J4.pin8, J5.pin8, J6.pin8, J2.pin8, J7.pin8
  N17: IC1.pin11, J3.pin9, J4.pin9, J5.pin9, J6.pin9, J2.pin9, J7.pin9
  N18: IC1.pin13, J3.pin10, J4.pin10, J5.pin10, J6.pin10, J2.pin10, J7.pin10
  N19: IC1.pin14, J3.pin11, J4.pin11, J5.pin11, J6.pin11, J2.pin11, J7.pin11
  N20: IC1.pin15, J3.pin4, J4.pin4, J5.pin4, J6.pin4, J2.pin4, J7.pin4
  N21: IC1.pin16, J3.pin5, J4.pin5, J5.pin5, J6.pin5, J2.pin5, J7.pin5
  N22: Q4.B, R6.Pin_1, R8.Pin_1
  N23: Q4.C, R7.Pin_0
  N24: R7.Pin_1, J3.pin1
  N25: Q6.B, R10.Pin_1, R12.Pin_1
  N26: Q6.C, R11.Pin_0
  N27: R11.Pin_1, J4.pin1
  N28: Q8.B, R14.Pin_1, R16.Pin_1
  N29: Q8.C, R15.Pin_0
  N30: R15.Pin_1, J5.pin1
  N31: Q10.B, R18.Pin_1, R20.Pin_1
  N32: Q10.C, R19.Pin_0
  N33: R19.Pin_1, J6.pin1
  N34: Q12.B, R22.Pin_1, R24.Pin_1
  N35: Q12.C, R23.Pin_0
  N36: R23.Pin_1, J7.pin1
