# Fritzing sketch Test-IC-Multiplexor (saved by Fritzing 0.9.2b)
breadboards: 1

parts:
  R1 = Trimmer Potentiometer [maximum_resistance=10kΩ package=THT]
  R2 = Resistor [tolerance=±5% resistance=6.8k package=THT]
  Power_plug1 = Power plug
  IC1 = IC, DIP package, 16 pins [chip_label=K155ID1]
  J1 = male pin header, 6 pins [form="♂ (male)"]
  C1 = Ceramic Capacitor [capacitance=100nF package="100 mil [THT, multilayer]"]
  Power_plug2 = Power plug
  Q3 = PNP-Transistor [part_number=mpsa92 package="TO92 [THT]"]
  Q4 = NPN-Transistor [part_number=mpsa42 package="TO92 [THT]"]
  R12 = Resistor [tolerance=±5% resistance=15k package=THT]
  R13 = Resistor [tolerance=±5% resistance=5.6k package=THT]
  R14 = Resistor [tolerance=±5% resistance=390k package=THT]
  R15 = Resistor [tolerance=±5% resistance=10k package=THT]

nets:
  N1: R1.wiper, R2.Pin_1
  N2: R1.leg2, J1.pin5
  N3: R2.Pin_0, J1.pin4
  GND: Power_plug1.GND, IC1.pin3, IC1.pin4, IC1.pin6, IC1.pin7, IC1.pin12, J1.pin2, J1.pin3, C1.1, Power_plug2.GND, Q4.E
  N4: Power_plug1.VCC, J1.pin1
  N5: IC1.pin5, C1.0, Power_plug2.VCC, R15.Pin_1
  N6: J1.pin6, Q3.E, R13.Pin_0
  N7: Q3.B, R13.Pin_1, R14.Pin_0
  N8: Q3.C, R12.Pin_1
  N9: Q4.B, R15.Pin_0
  N10: Q4.C, R14.Pin_1

notes:
  12 volts
  To Multimeter
  5 volts
