# Fritzing sketch Test-IC-Mux-Neon (saved by Fritzing 0.9.2b)
breadboards: 1

parts:
  R1 = Trimmer Potentiometer [maximum_resistance=10kΩ package=THT]
  R2 = Resistor [tolerance=±5% resistance=6.8k package=THT]
  Power_plug1 = Power plug
  IC1 = IC, DIP package, 16 pins [chip_label=K155ID1]
  J1 = male pin header, 6 pins [form="♂ (male)"]
  C1 = Ceramic Capacitor [capacitance=100nF package="100 mil [THT, multilayer]"]
  Power_plug2 = Power plug
  Q3 = PNP-Transistor [part_number=mpsa92 package="TO92 [THT]"]
  Q4 = NPN-Transistor [part_number=mpsa42 package="TO92 [THT]"]
  R12 = Resistor [tolerance=±5% resistance=390k package=THT]
  R13 = Resistor [tolerance=±5% resistance=5.6k package=THT]
  R14 = Resistor [tolerance=±5% resistance=390k package=THT]
  R15 = Resistor [tolerance=±5% resistance=10k package=THT]
  J2 = T Cobbler Plus
  NE-1 = Neon Bulb
  NE-2 = Neon Bulb
  NE-3 = Neon Bulb
  NE-4 = Neon Bulb
  NE-5 = Neon Bulb
  R17 = Resistor [tolerance=±5% resistance=390k package=THT]
  R18 = Resistor [tolerance=±5% resistance=390k package=THT]
  R19 = Resistor [tolerance=±5% resistance=390k package=THT]
  R20 = Resistor [tolerance=±5% resistance=390k package=THT]
  R21 = Resistor [tolerance=±5% resistance=390k package=THT]

nets:
  N1: R1.wiper, R2.Pin_1
  N2: R1.leg2, J1.pin5
  N3: R2.Pin_0, J1.pin4
  GND: Power_plug1.GND, IC1.pin12, J1.pin2, J1.pin3, C1.1, Power_plug2.GND, Q4.E, J2.SCLK
  N4: Power_plug1.VCC, J1.pin1
  N5: IC1.pin1, R18.Pin_0
  N6: IC1.pin2, R17.Pin_0
  N7: IC1.pin3, J2.#22
  N8: IC1.pin4, J2.#24
  N9: IC1.pin5, C1.0, J2.GND#8
  N10: IC1.pin6, J2.#23
  N11: IC1.pin7, J2.3.3V
  N12: IC1.pin8, NE-3.A
  N13: IC1.pin9, NE-4.A
  N14: IC1.pin10, R19.Pin_0
  N15: IC1.pin11, R20.Pin_0
  N16: IC1.pin13, NE-2.A
  N17: IC1.pin14, R21.Pin_0
  N18: IC1.pin15, NE-5.A
  N19: IC1.pin16, NE-1.A
  N20: J1.pin6, Q3.E, R13.Pin_0
  N21: Power_plug2.VCC, J2.#25
  N22: Q3.B, R13.Pin_1, R14.Pin_0
  N23: Q3.C, R12.Pin_1
  N24: Q4.B, R15.Pin_0
  N25: Q4.C, R14.Pin_1
  N26: R12.Pin_0, NE-1.B, NE-2.B, NE-3.B, NE-4.B, NE-5.B, R17.Pin_1, R18.Pin_1, R19.Pin_1, R20.Pin_1, R21.Pin_1
  N27: R15.Pin_1, J2.GND#5

notes:
  12 volts
  5 volts
  To Multimeter

custom parts:
  T Cobbler Plus: The T-Cobbler Plus is an add on prototyping board from Adafruit specifically designed for the Raspberry Pi B+ that can break out all those tasty power, GPIO, I2C and SPI pins from the 40-pin header onto a solderless breadboard. This set will make "cobbling together" prototypes with the Pi super easy. The T-Cobbler Plus can plug into any solderless breadboard.
  Neon Bulb: Neon bulb
