# Fritzing sketch Test-IC-Mux-Nixie (saved by Fritzing 0.9.2b)
breadboards: 1

parts:
  R1 = Trimmer Potentiometer [maximum_resistance=10kΩ package=THT]
  R2 = Resistor [tolerance=±5% resistance=6.8k package=THT]
  Power_plug1 = Power plug
  IC1 = IC, DIP package, 16 pins [chip_label=K155ID1]
  J1 = male pin header, 6 pins [form="♂ (male)"]
  C1 = Ceramic Capacitor [capacitance=100nF package="100 mil [THT, multilayer]"]
  Power_plug2 = Power plug
  Q3 = PNP-Transistor [part_number=mpsa92 package="TO92 [THT]"]
  Q4 = NPN-Transistor [part_number=mpsa42 package="TO92 [THT]"]
  R12 = Resistor [tolerance=±5% resistance=15k package=THT]
  R13 = Resistor [tolerance=±5% resistance=5.6k package=THT]
  R14 = Resistor [tolerance=±5% resistance=390k package=THT]
  R15 = Resistor [tolerance=±5% resistance=10k package=THT]
  J2 = T Cobbler Plus
  J3 = double row male pin header, 12 pins [form="♂ (male)"]

nets:
  N1: R1.wiper, R2.Pin_1
  N2: R1.leg2, J1.pin5
  N3: R2.Pin_0, J1.pin4
  GND: Power_plug1.GND, IC1.pin12, J1.pin2, J1.pin3, C1.1, Power_plug2.GND, Q4.E, J2.SCLK
  N4: Power_plug1.VCC, J1.pin1
  N5: IC1.pin1, J3.pin7
  N6: IC1.pin2, J3.pin6
  N7: IC1.pin3, J2.#22
  N8: IC1.pin4, J2.#24
  N9: IC1.pin5, C1.0, J2.GND#8
  N10: IC1.pin6, J2.#23
  N11: IC1.pin7, J2.3.3V
  N12: IC1.pin8, J3.pin3
  N13: IC1.pin9, J3.pin2
  N14: IC1.pin10, J3.pin8
  N15: IC1.pin11, J3.pin9
  N16: IC1.pin13, J3.pin10
  N17: IC1.pin14, J3.pin11
  N18: IC1.pin15, J3.pin4
  N19: J1.pin6, Q3.E, R13.Pin_0
  N20: Power_plug2.VCC, J2.#25
  N21: Q3.B, R13.Pin_1, R14.Pin_0
  N22: Q3.C, R12.Pin_1
  N23: Q4.B, R15.Pin_0
  N24: Q4.C, R14.Pin_1
  N25: R15.Pin_1, J2.GND#5

notes:
  12 volts
  Nixie Header
  5 volts
  To Multimeter

custom parts:
  T Cobbler Plus: The T-Cobbler Plus is an add on prototyping board from Adafruit specifically designed for the Raspberry Pi B+ that can break out all those tasty power, GPIO, I2C and SPI pins from the 40-pin header onto a solderless breadboard. This set will make "cobbling together" prototypes with the Pi super easy. The T-Cobbler Plus can plug into any solderless breadboard.
