# Fritzing sketch Test-Nixie (saved by Fritzing 0.9.2b)
breadboards: 1

parts:
  J1 = male pin header, 6 pins [form="♂ (male)"]
  Power_plug1 = Power plug
  R1 = Trimmer Potentiometer [maximum_resistance=10kΩ package=THT]
  R2 = Resistor [tolerance=±5% resistance=6.8k package=THT]
  R3 = Resistor [tolerance=±5% resistance=15k package=THT]

nets:
  N1: J1.pin1, Power_plug1.VCC
  N2: J1.pin2, J1.pin3, Power_plug1.GND
  N3: J1.pin4, R2.Pin_0
  N4: J1.pin5, R1.leg2
  N5: J1.pin6, R3.Pin_0
  N6: R1.wiper, R2.Pin_1

notes:
  To Multimeter
  To Nixie
  12 volts
