# Fritzing sketch Test-TCobb-LED-Multi (saved by Fritzing 0.9.2b)
breadboards: 1

parts:
  J1 = T Cobbler Plus
  LED1 = LED - 5mm [color="Red (633nm)" package="5 mm [THT]"]
  LED2 = LED - 5mm [color="Red (633nm)" package="5 mm [THT]"]
  LED3 = LED - 5mm [color="Red (633nm)" package="5 mm [THT]"]
  LED4 = LED - 5mm [color="Red (633nm)" package="5 mm [THT]"]
  LED5 = LED - 5mm [color="Red (633nm)" package="5 mm [THT]"]
  LED6 = LED - 5mm [color="Red (633nm)" package="5 mm [THT]"]
  R1 = Resistor [tolerance=±5% resistance=1k package=THT]
  R2 = Resistor [tolerance=±5% resistance=1k package=THT]
  R3 = Resistor [tolerance=±5% resistance=1k package=THT]
  R4 = Resistor [tolerance=±5% resistance=1k package=THT]
  R5 = Resistor [tolerance=±5% resistance=1k package=THT]
  R6 = Resistor [tolerance=±5% resistance=1k package=THT]
  LED7 = LED - 5mm [color="Green (565nm)" package="5 mm [THT]"]
  LED8 = LED - 5mm [color="Green (565nm)" package="5 mm [THT]"]
  LED9 = LED - 5mm [color="Green (565nm)" package="5 mm [THT]"]
  LED10 = LED - 5mm [color="Green (565nm)" package="5 mm [THT]"]
  R7 = Resistor [tolerance=±5% resistance=1k package=THT]
  R8 = Resistor [tolerance=±5% resistance=1k package=THT]
  R9 = Resistor [tolerance=±5% resistance=1k package=THT]
  R10 = Resistor [tolerance=±5% resistance=1k package=THT]

nets:
  N1: J1.GND#5, LED1.anode
  N2: J1.#4, LED3.anode
  N3: J1.TXD, LED4.anode
  N4: J1.#22, LED7.anode
  N5: J1.#23, LED8.anode
  N6: J1.3.3V, LED9.anode
  N7: J1.#24, LED10.anode
  N8: J1.SCLK, R1.Pin_1, R2.Pin_1, R3.Pin_1, R4.Pin_1, R5.Pin_1, R6.Pin_1, R7.Pin_1, R8.Pin_1, R9.Pin_1, R10.Pin_1
  N9: J1.CE1, LED2.anode
  N10: J1.EEC, LED5.anode
  N11: J1.#5, LED6.anode
  N12: LED1.cathode, R1.Pin_0
  N13: LED2.cathode, R2.Pin_0
  N14: LED3.cathode, R3.Pin_0
  N15: LED4.cathode, R4.Pin_0
  N16: LED5.cathode, R5.Pin_0
  N17: LED6.cathode, R6.Pin_0
  N18: LED7.cathode, R7.Pin_0
  N19: LED8.cathode, R8.Pin_0
  N20: LED9.cathode, R9.Pin_0
  N21: LED10.cathode, R10.Pin_0

notes:
  5 volts

custom parts:
  T Cobbler Plus: The T-Cobbler Plus is an add on prototyping board from Adafruit specifically designed for the Raspberry Pi B+ that can break out all those tasty power, GPIO, I2C and SPI pins from the 40-pin header onto a solderless breadboard. This set will make "cobbling together" prototypes with the Pi super easy. The T-Cobbler Plus can plug into any solderless breadboard.
